# Fritzing sketch Garo GM3D PCB (saved by Fritzing 0.9.2b)
circuit board: 6.19799cm x 2.95112cm
breadboards: 1

parts:
  Raspberry_Pi = Cobbler Plus
  R1_-_10k = Resistor [tolerance=±5% resistance=10k package=THT]
  R1_-_1k = Resistor [tolerance=±5% resistance=10k package=THT]
  JP1 = Header 2 [package=screwterminal-3.5mm-2_lock]

nets:
  N1: Raspberry_Pi.3V3, JP1.1
  N2: Raspberry_Pi.GND, R1_-_10k.Pin_0
  N3: Raspberry_Pi.#17, R1_-_1k.Pin_0
  N4: R1_-_10k.Pin_1, R1_-_1k.Pin_1, JP1.2

notes:
  GND
  Right
  Left Out
  Spk. 1
  Left In
  Left In   Left Out
  Red White   Red White
  VCC

custom parts:
  Cobbler Plus: The Cobbler Plus is an add on prototyping board from Adafruit specifically designed for the Raspberry Pi B+ that can break out all those tasty power, GPIO, I2C and SPI pins from the 40-pin header onto a solderless breadboard. This set will make "cobbling together" prototypes with the Pi super easy. The Cobbler Plus can plug into any solderless breadboard.
